# Fritzing sketch spotmicroai (saved by Fritzing 0.9.10b)

parts:
  Mod2 = Raspberry Pi 4B
  PWM2 = PCA9685 16x12-bit PWM Breakout
  부품2 = InvenSense MPU6050

nets:
  N1: Mod2.3V3, PWM2.no_name_yet#505
  5V: Mod2.5V, 부품2.VCC
  N2: Mod2.GPIO2, PWM2.no_name_yet#504, 부품2.SDA
  N3: Mod2.GPIO3, PWM2.no_name_yet#503, 부품2.SCL
  GND: Mod2.GND, PWM2.no_name_yet#501, 부품2.GND

notes:
  +5V DC
